# Fritzing sketch Untitled Sketch (saved by Fritzing 0.9.3b)
circuit board: 10.197cm x 5.46679cm

parts:
  JP1 = Header 2 [package=molex-1x2_lock]
  M1 = Header 1 [package=1x01_offset]
  M2 = Header 1 [package=1x01_offset]
  M3 = Header 1 [package=1x01_offset]
  M4 = Header 1 [package=1x01_offset]
  P4 = Header 1 [package=1x01_offset]
  P1 = Header 1 [package=1x01_offset]
  P2 = Header 1 [package=1x01_offset]
  P3 = Header 1 [package=1x01_offset]
  FCA = Header 2 [package=molex-1x2_lock]
  FCR = Header 2 [package=molex-1x2_lock]
  modo = Header 2 [package=molex-1x2_lock]
  paro = Header 2 [package=molex-1x2_lock]
  next = Header 2 [package=molex-1x2_lock]
  Avance = Header 2 [package=molex-1x2_lock]
  Regreso = Header 2 [package=molex-1x2_lock]
  Corte = Header 2 [package=molex-1x2_lock]
  op8 = Header 2 [package=molex-1x2_lock]
  op6 = Header 2 [package=molex-1x2_lock]
  op7 = Header 2 [package=molex-1x2_lock]
  op2 = Header 2 [package=molex-1x2_lock]
  op5 = Header 2 [package=molex-1x2_lock]
  op1 = Header 2 [package=molex-1x2_lock]
  op3 = Header 2 [package=molex-1x2_lock]
  op4 = Header 2 [package=molex-1x2_lock]
  op9 = Header 2 [package=molex-1x2_lock]
  op10 = Header 2 [package=molex-1x2_lock]
  O_PE = Sharp PC817 [package=THT]
  O_PP = Sharp PC817 [package=THT]
  O_PD = Sharp PC817 [package=THT]
  M_P+ = Sharp PC817 [package=THT]
  M_P- = Sharp PC817 [package=THT]
  M_D- = Sharp PC817 [package=THT]
  S1 = Toggle Switch [package=THT]
  S2 = Toggle Switch [package=THT]
  S3 = Toggle Switch [package=THT]
  S4 = Toggle Switch [package=THT]
  S5 = Toggle Switch [package=THT]
  S6 = Toggle Switch [package=THT]
  L1 = smd LED [color="Green (570nm)" package="0805 [SMD]"]
  R2 = Resistor [tolerance=±5% resistance=2.2k package="0805 [SMD]"]
  R1 = Resistor [tolerance=±5% resistance=2.2k package="0805 [SMD]"]
  R3 = Resistor [tolerance=±5% resistance=2.2k package="0805 [SMD]"]
  R4 = Resistor [tolerance=±5% resistance=2.2k package="0805 [SMD]"]
  L2 = smd LED [color="Green (570nm)" package="0805 [SMD]"]
  R5 = Resistor [tolerance=±5% resistance=2.2k package="0805 [SMD]"]
  R6 = Resistor [tolerance=±5% resistance=2.2k package="0805 [SMD]"]
  L3 = smd LED [color="Green (570nm)" package="0805 [SMD]"]
  R7 = Resistor [tolerance=±5% resistance=2.2k package="0805 [SMD]"]
  R8 = Resistor [tolerance=±5% resistance=2.2k package="0805 [SMD]"]
  L4 = smd LED [color="Green (570nm)" package="0805 [SMD]"]
  R9 = Resistor [tolerance=±5% resistance=2.2k package="0805 [SMD]"]
  R10 = Resistor [tolerance=±5% resistance=2.2k package="0805 [SMD]"]
  L5 = smd LED [color="Green (570nm)" package="0805 [SMD]"]
  R11 = Resistor [tolerance=±5% resistance=2.2k package="0805 [SMD]"]
  R12 = Resistor [tolerance=±5% resistance=2.2k package="0805 [SMD]"]
  L6 = smd LED [color="Green (570nm)" package="0805 [SMD]"]
  Componente3 = Arduino Due (Rev2b)

nets:
  N1: JP1.1, Componente3.MASTER-RESET
  N2: JP1.2, FCA.2, FCR.2, modo.2, paro.2, next.2, Avance.2, Regreso.2, Corte.2, op8.2, op6.2, op7.2, op2.2, op5.2, op1.2, op3.2, op4.2, op9.2, op10.2, R2.Pin_1, R1.Pin_0, R3.Pin_0, R4.Pin_1, R5.Pin_0, R6.Pin_1, R7.Pin_0, R8.Pin_1, R9.Pin_0, R10.Pin_1, R11.Pin_0, R12.Pin_1, Componente3.GND
  N3: M1.1, P1.1, O_PE.Pin_4, O_PP.Pin_4, O_PD.Pin_4, M_P+.Pin_4, M_P-.Pin_4, M_D-.Pin_4, Componente3.5V
  N4: M2.1, S1.COM
  N5: M3.1, S2.COM
  N6: M4.1, S3.COM
  N7: P4.1, S6.COM
  N8: P2.1, S4.COM
  N9: P3.1, S5.COM
  N10: FCA.1, Componente3.D9_PWM
  N11: FCR.1, Componente3.D8_PWM
  N12: modo.1, Componente3.D7_PWM
  N13: paro.1, Componente3.D6_PWM
  N14: next.1, Componente3.D5_PWM
  N15: Avance.1, Componente3.D4_PWM/SS1
  N16: Regreso.1, Componente3.D3_PWM
  N17: Corte.1, Componente3.D2_PWM
  N18: op8.1, Componente3.D38
  N19: op6.1, Componente3.D36
  N20: op7.1, Componente3.D28
  N21: op2.1, Componente3.D32
  N22: op5.1, Componente3.D26
  N23: op1.1, Componente3.D22
  N24: op3.1, Componente3.D24
  N25: op4.1, Componente3.D34
  N26: op9.1, Componente3.D30
  N27: op10.1, Componente3.D40
  N28: O_PE.Pin_1, S6.L1, Componente3.D14/TX3
  N29: O_PE.Pin_2, L6.anode
  N30: O_PE.Pin_3, S6.L2, R12.Pin_0
  N31: O_PP.Pin_1, S5.L1, Componente3.D17/RX2
  N32: O_PP.Pin_2, L5.anode
  N33: O_PP.Pin_3, S5.L2, R10.Pin_0
  N34: O_PD.Pin_1, S4.L1, Componente3.D16/TX2
  N35: O_PD.Pin_2, L4.anode
  N36: O_PD.Pin_3, S4.L2, R8.Pin_0
  N37: M_P+.Pin_1, S3.L1, Componente3.D12_PWM
  N38: M_P+.Pin_2, L1.anode
  N39: M_P+.Pin_3, S3.L2, R2.Pin_0
  N40: M_P-.Pin_1, S2.L1, Componente3.D11_PWM
  N41: M_P-.Pin_2, L2.anode
  N42: M_P-.Pin_3, S2.L2, R4.Pin_0
  N43: M_D-.Pin_1, S1.L1, Componente3.D10_PWM/SS0
  N44: M_D-.Pin_2, L3.anode
  N45: M_D-.Pin_3, S1.L2, R6.Pin_0
  N46: L1.cathode, R1.Pin_1
  N47: R3.Pin_1, L2.cathode
  N48: R5.Pin_1, L3.cathode
  N49: R7.Pin_1, L4.cathode
  N50: R9.Pin_1, L5.cathode
  N51: R11.Pin_1, L6.cathode
